// Logisim project Russian.circ as structural Verilog: 3 circuits, main circuit main
module main (
);

  wire and_1_out, and_2_out, and_3_out, and_4_out, and_5_out, and_6_out, and_7_out, and_8_out, Bullet_out,
       counter_2_a, counter_2_b, counter_3_a, counter_3_b, counter_4_a, counter_4_b, counter_a, counter_b,
       d_ff_1_q, d_ff_2_q, d_ff_3_q, d_ff_4_q, n7segment_1_a_2, n7segment_1_b_2, n7segment_1_c_2,
       n7segment_1_d_2, n7segment_1_e, n7segment_1_f, n7segment_1_g, n7segment_2_a_2, n7segment_2_b_2,
       n7segment_2_c_2, n7segment_2_d_2, n7segment_2_e, n7segment_2_f, n7segment_2_g, n7segment_3_a_2,
       n7segment_3_b_2, n7segment_3_c_2, n7segment_3_d_2, n7segment_3_e, n7segment_3_f, n7segment_3_g,
       n7segment_4_a_2, n7segment_4_b_2, n7segment_4_c_2, n7segment_4_d_2, n7segment_4_e, n7segment_4_f,
       n7segment_4_g, nor_1_out, nor_2_out, nor_3_out, nor_4_out, or_1_out, Reset_out, Trigger_out;

  Button Reset (.out(Reset_out));
  _7_Segment_Display u_7_segment_display_1 (
    .g(n7segment_1_g), .f(n7segment_1_f), .a(n7segment_1_a_2), .b(n7segment_1_b_2), .e(n7segment_1_e),
    .d(n7segment_1_d_2), .c(n7segment_1_c_2));  // open: dp
  _7segment u_7segment_1 (
    .A(1'b0), .B(1'b0), .C(counter_b), .D(counter_a), .a_2(n7segment_1_a_2), .b_2(n7segment_1_b_2),
    .c_2(n7segment_1_c_2), .d_2(n7segment_1_d_2), .e(n7segment_1_e), .f(n7segment_1_f), .g(n7segment_1_g));
  counter counter (.Clk(and_3_out), .reset(Reset_out), .a(counter_a), .b(counter_b));
  Button Trigger (.out(Trigger_out));
  nor nor_1 (nor_1_out, counter_a, counter_b);
  Shift_Register #(.length(7)) Bullet (
    .in(Bullet_out), .clk(Trigger_out), .out(Bullet_out), .clr(Reset_out));  // open: shift, load, d0, q0, d1, q1, d2, q2, d3, q3, d4, q4, d5, q5, d6, q6
  LED led_1 (.in(and_1_out));
  and and_1 (and_1_out, nor_1_out, and_3_out);
  _7_Segment_Display u_7_segment_display_2 (
    .g(n7segment_2_g), .f(n7segment_2_f), .a(n7segment_2_a_2), .b(n7segment_2_b_2), .e(n7segment_2_e),
    .d(n7segment_2_d_2), .c(n7segment_2_c_2));  // open: dp
  _7segment u_7segment_2 (
    .A(1'b0), .B(1'b0), .C(counter_2_b), .D(counter_2_a), .a_2(n7segment_2_a_2), .b_2(n7segment_2_b_2),
    .c_2(n7segment_2_c_2), .d_2(n7segment_2_d_2), .e(n7segment_2_e), .f(n7segment_2_f), .g(n7segment_2_g));
  counter counter_2 (.Clk(and_4_out), .reset(Reset_out), .a(counter_2_a), .b(counter_2_b));
  LED led_2 (.in(and_2_out));
  and and_2 (and_2_out, nor_2_out, and_4_out);
  nor nor_2 (nor_2_out, counter_2_a, counter_2_b);
  or or_1 (or_1_out, Bullet_out, Bullet_out);
  _7segment u_7segment_3 (
    .A(1'b0), .B(1'b0), .C(counter_3_b), .D(counter_3_a), .a_2(n7segment_3_a_2), .b_2(n7segment_3_b_2),
    .c_2(n7segment_3_c_2), .d_2(n7segment_3_d_2), .e(n7segment_3_e), .f(n7segment_3_f), .g(n7segment_3_g));
  and and_3 (and_3_out, or_1_out, d_ff_1_q);
  D_Flip_Flop d_ff_1 (.clk(Trigger_out), .D(d_ff_4_q), .Q(d_ff_1_q), .preset(Reset_out));  // open: Qn, en, reset
  _7_Segment_Display u_7_segment_display_3 (
    .g(n7segment_3_g), .f(n7segment_3_f), .a(n7segment_3_a_2), .b(n7segment_3_b_2), .e(n7segment_3_e),
    .d(n7segment_3_d_2), .c(n7segment_3_c_2));  // open: dp
  counter counter_3 (.Clk(and_6_out), .reset(Reset_out), .a(counter_3_a), .b(counter_3_b));
  and and_4 (and_4_out, or_1_out, d_ff_2_q);
  D_Flip_Flop d_ff_2 (.clk(Trigger_out), .D(d_ff_1_q), .Q(d_ff_2_q), .reset(Reset_out));  // open: Qn, preset, en
  LED led_3 (.in(and_5_out));
  and and_5 (and_5_out, nor_3_out, and_6_out);
  nor nor_3 (nor_3_out, counter_3_a, counter_3_b);
  and and_6 (and_6_out, or_1_out, d_ff_3_q);
  D_Flip_Flop d_ff_3 (.clk(Trigger_out), .D(d_ff_2_q), .Q(d_ff_3_q), .reset(Reset_out));  // open: Qn, preset, en
  _7segment u_7segment_4 (
    .A(1'b0), .B(1'b0), .C(counter_4_b), .D(counter_4_a), .a_2(n7segment_4_a_2), .b_2(n7segment_4_b_2),
    .c_2(n7segment_4_c_2), .d_2(n7segment_4_d_2), .e(n7segment_4_e), .f(n7segment_4_f), .g(n7segment_4_g));
  and and_7 (and_7_out, or_1_out, d_ff_4_q);
  D_Flip_Flop d_ff_4 (.clk(Trigger_out), .D(d_ff_3_q), .Q(d_ff_4_q), .reset(Reset_out));  // open: Qn, preset, en
  _7_Segment_Display u_7_segment_display_4 (
    .g(n7segment_4_g), .f(n7segment_4_f), .a(n7segment_4_a_2), .b(n7segment_4_b_2), .e(n7segment_4_e),
    .d(n7segment_4_d_2), .c(n7segment_4_c_2));  // open: dp
  counter counter_4 (.Clk(and_7_out), .reset(Reset_out), .a(counter_4_a), .b(counter_4_b));
  LED led_4 (.in(and_8_out));
  and and_8 (and_8_out, nor_4_out, and_7_out);
  nor nor_4 (nor_4_out, counter_4_a, counter_4_b);

  // Notes on the sheet:
  //   19011502 Rak-won Choi Project
  //   Russian roulette game
  //   Number of times each player lost
  //   Player 1 Lose!!
  //   Player 2 Lose!!
  //   Player 3 Lose!!
  //   Player 4 Lose!!
endmodule

module _7segment (
  input  A,
  input  B,
  input  C,
  input  D,
  output a_2,
  output b_2,
  output c_2,
  output d_2,
  output e,
  output f,
  output g
);

  wire and_1_out, and_2_out, and_3_out, and_4_out, and_5_out, and_6_out, and_7_out, and_8_out, and_9_out,
       and_10_out, and_11_out, and_12_out, and_13_out, and_14_out, and_15_out, and_16_out, not_1_out,
       not_2_out, not_3_out, not_4_out, not_5_out, not_6_out, not_7_out, not_8_out, not_9_out, not_10_out,
       not_11_out, not_12_out, not_13_out, not_14_out, not_15_out, not_16_out, not_17_out, not_18_out,
       not_19_out, not_20_out, not_21_out;

  not not_1 (not_1_out, B);
  not not_2 (not_2_out, D);
  not not_3 (not_3_out, B);
  not not_4 (not_4_out, D);
  not not_5 (not_5_out, C);
  not not_6 (not_6_out, B);
  not not_7 (not_7_out, D);
  not not_8 (not_8_out, C);
  not not_9 (not_9_out, D);
  not not_10 (not_10_out, C);
  not not_11 (not_11_out, D);
  not not_12 (not_12_out, B);
  and and_1 (and_1_out, not_1_out, not_2_out);
  and and_2 (and_2_out, B, D);
  not not_13 (not_13_out, B);
  not not_14 (not_14_out, C);
  and and_3 (and_3_out, not_14_out, not_15_out);
  not not_15 (not_15_out, D);
  and and_4 (and_4_out, C, D);
  not not_16 (not_16_out, C);
  not not_17 (not_17_out, B);
  and and_5 (and_5_out, not_17_out, not_18_out);
  not not_18 (not_18_out, D);
  and and_6 (and_6_out, not_3_out, C);
  and and_7 (and_7_out, C, not_4_out);
  and and_8 (and_8_out, B, not_5_out, D);
  and and_9 (and_9_out, not_6_out, not_7_out);
  and and_10 (and_10_out, C, not_19_out);
  not not_19 (not_19_out, D);
  not not_20 (not_20_out, C);
  and and_11 (and_11_out, not_20_out, not_21_out);
  not not_21 (not_21_out, D);
  and and_12 (and_12_out, B, not_8_out);
  and and_13 (and_13_out, B, not_9_out);
  and and_14 (and_14_out, B, not_10_out);
  and and_15 (and_15_out, C, not_11_out);
  and and_16 (and_16_out, C, not_12_out);
  or or_1 (a_2, and_1_out, C, and_2_out, A);
  or or_2 (b_2, not_13_out, and_3_out, and_4_out);
  or or_3 (c_2, not_16_out, B, D);
  or or_4 (d_2, A, and_5_out, and_6_out, and_7_out, and_8_out);
  or or_5 (e, and_9_out, and_10_out);
  or or_6 (f, B, and_11_out, and_12_out, and_13_out);
  or or_7 (g, and_14_out, and_15_out, and_16_out, A);
endmodule

module counter (
  input  Clk,
  input  reset,
  output a,
  output b
);

  wire and_1_out, or_1_out;

  J_K_Flip_Flop u_A (.J(1'b1), .clk(Clk), .K(1'b1), .Q(a), .reset(or_1_out));  // open: Qn, preset, en
  J_K_Flip_Flop u_B (.J(a), .clk(Clk), .K(a), .Q(b), .reset(or_1_out));  // open: Qn, preset, en
  or or_1 (or_1_out, and_1_out, reset);
  and and_1 (and_1_out, a, b);

  // Notes on the sheet:
  //   A counter that counts to two and returns to zero
  //   Initialize to 0 when the reset button is pressed
endmodule
